# Fritzing sketch Anschlüsse (saved by Fritzing 0.9.3b)
breadboards: 1

parts:
  Bauteil1 = Arduino Uno (Rev3)
  LCD1 = LCD screen
  R1 = Rotary Potentiometer (Small) [maximum_resistance=10kΩ package=THT]
  S1 = Pushbutton [package="[THT]"]
  R2 = Resistor [tolerance=±5% resistance=10k package=THT]
  C1 = Electrolytic Capacitor [capacitance=1µF package="100 mil [THT, electrolytic]"]
  C2 = Electrolytic Capacitor [capacitance=1µF package="100 mil [THT, electrolytic]"]
  MPXH1 = Drucksensor MPXH 6115AC6U [package=THT]
  MPXH = Drucksensor MPXH 6115AC6U [package=THT]
  C3 = Electrolytic Capacitor [capacitance=1µF package="100 mil [THT, electrolytic]"]

nets:
  N1: Bauteil1.A0, MPXH.Vs, C3.+
  N2: Bauteil1.A1, C1.+, MPXH1.Vs
  N3: Bauteil1.D8, LCD1.E
  N4: Bauteil1.D9_PWM, LCD1.DB4
  N5: Bauteil1.D10_PWM/SS, LCD1.DB5
  N6: Bauteil1.D11_PWM/MOSI, LCD1.DB6
  N7: Bauteil1.D12/MISO, LCD1.DB7
  GND: Bauteil1.GND, LCD1.VSS, LCD1.R/W, LCD1.LED-, R1.leg1, R2.Pin_1, C1.-, C2.+, MPXH1.GND, MPXH.GND, C3.-
  N8: Bauteil1.D7, LCD1.RS
  5V: Bauteil1.5V, LCD1.VDD, LCD1.LED+, R1.leg2, S1.Pin_3, S1.Pin_4, C2.-, MPXH1.Vout, MPXH.Vout
  N9: LCD1.V0, R1.wiper
  N10: S1.Pin_1, S1.Pin_2, R2.Pin_0

custom parts:
  Drucksensor MPXH 6115AC6U: A dummy for a MPXH 6115AC6U pressure Sensor
