# Fritzing sketch Platinen kompatibel schaltplan (saved by Fritzing 0.9.3b)
breadboards: 1

parts:
  Bauteil1 = Arduino Uno (Rev3)
  LCD1 = LCD screen
  R2 = Rotary Potentiometer (Small) [maximum_resistance=10kΩ package=THT]
  Misst_Luftdruck2 = Drucksensor MPXH 6115AC6U [package=THT]
  C1 = Electrolytic Capacitor [capacitance=1µF package="100 mil [THT, electrolytic]"]
  C2 = Electrolytic Capacitor [capacitance=1µF package="100 mil [THT, electrolytic]"]
  C3 = Electrolytic Capacitor [capacitance=1µF package="100 mil [THT, electrolytic]"]
  Misst_Luftdruck1 = Drucksensor MPXH 6115AC6U [package=THT]
  R3 = Resistor [tolerance=±5% resistance=220 package=THT]
  S1 = Pushbutton [package="[THT]"]

nets:
  N1: Bauteil1.A0, C1.+, Misst_Luftdruck1.Vout
  N2: Bauteil1.A1, Misst_Luftdruck2.Vout, C2.+
  N3: Bauteil1.D8, LCD1.E
  N4: Bauteil1.D9_PWM, LCD1.DB4
  N5: Bauteil1.D10_PWM/SS, LCD1.DB5
  N6: Bauteil1.D11_PWM/MOSI, LCD1.DB6
  N7: Bauteil1.D12/MISO, LCD1.DB7
  N8: Bauteil1.D13/SCK, R3.Pin_1, S1.Pin_3, S1.Pin_4
  GND: Bauteil1.GND, LCD1.VSS, LCD1.R/W, LCD1.LED-, R2.leg1, Misst_Luftdruck2.GND, C1.-, C2.-, C3.-, Misst_Luftdruck1.GND, R3.Pin_0
  N9: Bauteil1.D7, LCD1.RS
  5V: Bauteil1.5V, LCD1.VDD, LCD1.LED+, R2.leg2, Misst_Luftdruck2.Vs, C3.+, Misst_Luftdruck1.Vs, S1.Pin_1, S1.Pin_2
  N10: LCD1.V0, R2.wiper

custom parts:
  Drucksensor MPXH 6115AC6U: A dummy for a MPXH 6115AC6U pressure Sensor
