# Fritzing sketch Platinen fertig (saved by Fritzing 0.9.3b)
circuit board: 6.88566cm x 5.36311cm
breadboards: 1

parts:
  LCD1 = LCD screen
  R2 = Rotary Potentiometer (Small) [maximum_resistance=10kΩ package=THT]
  Misst_Luftdruck2 = Drucksensor MPXH 6115AC6U [package=THT]
  C1 = Electrolytic Capacitor [capacitance=47pF package="100 mil [THT, electrolytic]"]
  C2 = Electrolytic Capacitor [capacitance=47pF package="100 mil [THT, electrolytic]"]
  C3 = Electrolytic Capacitor [capacitance=100nF package="100 mil [THT, electrolytic]"]
  Misst_Luftdruck1 = Drucksensor MPXH 6115AC6U [package=THT]
  R3 = Resistor [tolerance=±5% resistance=10k package=THT]
  S1 = Pushbutton [package="[THT]"]
  Bauteil1 = Arduino Uno (Rev3)
  J1 = female pin header, 1 pin [form="♀ (female)"]
  J2 = female pin header, 1 pin [form="♀ (female)"]
  J3 = female pin header, 1 pin [form="♀ (female)"]
  J4 = female pin header, 1 pin [form="♀ (female)"]
  R4 = Resistor [tolerance=±5% resistance=51k package=THT]
  R5 = Resistor [tolerance=±5% resistance=51k package=THT]

nets (from the pcb view):
  GND: LCD1.VSS, LCD1.LED-, Misst_Luftdruck2.GND, C1.-, C2.-, Misst_Luftdruck1.GND, R3.Pin_0, Bauteil1.GND, J4.pin1, R4.Pin_0, R5.Pin_0
  VDD: LCD1.VDD, LCD1.LED+, R2.leg2, Misst_Luftdruck2.Vs, C3.+, Misst_Luftdruck1.Vs, S1.Pin_1, S1.Pin_2, Bauteil1.5V
  N1: LCD1.V0, R2.wiper
  N2: LCD1.RS, Bauteil1.D7
  N3: LCD1.R/W, R2.leg1, C3.-, J3.pin1
  N4: LCD1.E, Bauteil1.D8
  N5: LCD1.DB4, Bauteil1.D9_PWM
  N6: LCD1.DB5, Bauteil1.D10_PWM/SS
  N7: LCD1.DB6, Bauteil1.D11_PWM/MOSI
  N8: LCD1.DB7, Bauteil1.D12/MISO
  N9: Misst_Luftdruck2.Vout, C2.+, Bauteil1.A1, R5.Pin_1
  N10: C1.+, Misst_Luftdruck1.Vout, Bauteil1.A0, R4.Pin_1
  N11: R3.Pin_1, S1.Pin_3, S1.Pin_4, J2.pin1
  N12: Bauteil1.D13/SCK, J1.pin1

custom parts:
  Drucksensor MPXH 6115AC6U: A dummy for a MPXH 6115AC6U pressure Sensor
