# Fritzing sketch Platinen kompatibel (saved by Fritzing 0.9.3b)
circuit board: 6.88566cm x 5.36311cm
breadboards: 1

parts:
  LCD1 = LCD screen
  R2 = Rotary Potentiometer (Small) [maximum_resistance=10kΩ package=THT]
  Misst_Luftdruck2 = Drucksensor MPXH 6115AC6U [package=THT]
  C1 = Electrolytic Capacitor [capacitance=1µF package="100 mil [THT, electrolytic]"]
  C2 = Electrolytic Capacitor [capacitance=1µF package="100 mil [THT, electrolytic]"]
  C3 = Electrolytic Capacitor [capacitance=1µF package="100 mil [THT, electrolytic]"]
  Misst_Luftdruck1 = Drucksensor MPXH 6115AC6U [package=THT]
  R3 = Resistor [tolerance=±5% resistance=220 package=THT]
  S1 = Pushbutton [package="[THT]"]
  Bauteil1 = Arduino Uno (Rev3)

nets:
  GND: LCD1.VSS, LCD1.R/W, LCD1.LED-, R2.leg1, Misst_Luftdruck2.GND, C1.-, C2.-, C3.-, Misst_Luftdruck1.GND, R3.Pin_0, Bauteil1.GND
  VDD: LCD1.VDD, LCD1.LED+, R2.leg2, Misst_Luftdruck2.Vs, C3.+, Misst_Luftdruck1.Vs, S1.Pin_1, S1.Pin_2, Bauteil1.5V
  N1: LCD1.V0, R2.wiper
  N2: LCD1.RS, Bauteil1.D7
  N3: LCD1.E, Bauteil1.D8
  N4: LCD1.DB4, Bauteil1.D9_PWM
  N5: LCD1.DB5, Bauteil1.D10_PWM/SS
  N6: LCD1.DB6, Bauteil1.D11_PWM/MOSI
  N7: LCD1.DB7, Bauteil1.D12/MISO
  N8: Misst_Luftdruck2.Vout, C2.+, Bauteil1.A1
  N9: C1.+, Misst_Luftdruck1.Vout, Bauteil1.A0
  N10: R3.Pin_1, S1.Pin_3, S1.Pin_4, Bauteil1.D13/SCK

custom parts:
  Drucksensor MPXH 6115AC6U: A dummy for a MPXH 6115AC6U pressure Sensor
